// Digital circuit 4-bit-processor_v2.dig as structural Verilog
module _4_bit_processor_v2 (
);

  Register_Files register_files_1 ();  // open: Clock, Read_Register_1, Read_Register_2, Control_Signal, Write_Register, Write_Data, Read_Data_1, Read_Data_2
  ALU_7Function alu_7function_1 ();  // open: A, B, S_1_S_0__C_in, D, Carry_Out
endmodule
