// Digital circuit 1BitAdder.dig as structural Verilog
module _1BitAdder (
  input  A,
  input  B,
  input  C,
  output Y,
  output Y_2
);

  wire and_1_out, and_2_out, xor_1_out;

  xor xor_1 (xor_1_out, A, B);
  and and_1 (and_1_out, A, B);
  xor xor_2 (Y, xor_1_out, C);
  and and_2 (and_2_out, xor_1_out, C);
  or or_1 (Y_2, and_1_out, and_2_out);
endmodule
