// Digital circuit Oct272025_Participation_AdderSubtractor.dig as structural Verilog
module Oct272025_Participation_AdderSubtractor (
  input  [3:0] A,
  input  [3:0] B,
  input  Add_Subtract,
  output [3:0] Sum,
  output Carry_Out
);

  wire add_2_c_o, add_3_c_o, add_4_c_o, xor_1_out, xor_2_out, xor_3_out, xor_4_out;

  xor xor_1 (xor_1_out, B[0], Add_Subtract);
  xor xor_2 (xor_2_out, B[1], Add_Subtract);
  xor xor_3 (xor_3_out, B[2], Add_Subtract);
  xor xor_4 (xor_4_out, B[3], Add_Subtract);
  Add add_1 (.a(A[3]), .b(xor_4_out), .c_i(add_2_c_o), .s(Sum[3]), .c_o(Carry_Out));
  Add add_2 (.a(A[2]), .b(xor_3_out), .c_i(add_3_c_o), .s(Sum[2]), .c_o(add_2_c_o));
  Add add_3 (.a(A[1]), .b(xor_2_out), .c_i(add_4_c_o), .s(Sum[1]), .c_o(add_3_c_o));
  Add add_4 (.a(A[0]), .b(xor_1_out), .c_i(Add_Subtract), .s(Sum[0]), .c_o(add_4_c_o));

  // Notes on the sheet:
  //   Add_Subtract: 0 = Add
  //   1 = Subtract
endmodule
